# Fritzing sketch acessibilidade (saved by Fritzing 0.9.3b)
circuit board: 8.46667cm x 5.64444cm

parts:
  DFPlayer_Mini1 = DFPlayer MINI [package="DIP (Dual Inline) [THT]"]
  U1 = ESP32S-HiLetgo [part_number=ESP32S]
  TRS1 = Audio Jack (TRS) 3.5mm [package="4Ucon 08780 [THT]"]
  R1 = Resistor [tolerance=±5% resistance=1M package=THT]

nets:
  N1: DFPlayer_Mini1.VCC, U1.3.3
  N2: DFPlayer_Mini1.RX, U1.GPIO17, R1.Pin_1
  N3: DFPlayer_Mini1.TX, U1.GPIO16
  N4: DFPlayer_Mini1.SPK1, TRS1.Ring
  GND: DFPlayer_Mini1.GND, U1.GND, TRS1.Sleeve, R1.Pin_0
  N5: DFPlayer_Mini1.SPK2, TRS1.Tip
  N6: DFPlayer_Mini1.IO_1, DFPlayer_Mini1.IO_2, DFPlayer_Mini1.K1/ADC_KEY, DFPlayer_Mini1.USB_+

custom parts:
  DFPlayer MINI: MP3 module by DFRobot.com for playing Music from an SD-Card. Supports WAV and MP3 files.
  ESP32S-HiLetgo: HiLetgo ESP-WROOM-32 ESP32 ESP-32S Development Board 2.4GHz Dual-Mode WiFi + Bluetooth Dual Cores Microcontroller The ESP32 integrated with Antenna switches, RF Balun, power amplifiers, low-noise amplifiers, filters, and management modules, and the entire solution occupies the least area of PCB. 2.4 GHz Wi-Fi plus Bluetooth dual-mode chip, with TSMC Ultra-low power consumption 40nm technology,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
